// Logisim project counter.circ as structural Verilog: 1 circuit, main circuit main
module main (
  input  Reset,
  output [3:0] Count
);

  wire clock_1_out;

  Clock clock_1 (.out(clock_1_out));
  // TclGeneric #(.filePath("counter.tcl"), .content("entity counter is port(sysclk_i : in std_logic; rst_i : in std_logic; cpt_o : out std_logic_vector(3 downto 0)); end counter;")) Safe_Tcl_counter: pin names not known; wires that end beside it: clock_1_out, Reset, Count
endmodule
