// Logisim project gray-two-counters.circ as structural Verilog: 1 circuit, main circuit main
module main (
  input  A,
  input  B,
  output [3:0] X,
  output [3:0] Y
);

  // Gray_Counter gray_counter_1: pin names not known; wires that end beside it: A, X
  // Gray_Counter gray_counter_2: pin names not known; wires that end beside it: B, Y
endmodule
