// Logisim project jar-drive-contention.circ as structural Verilog: 1 circuit, main circuit main
module main (
  input  A,
  input  EA,
  input  B,
  input  EB,
  output Y
);

  // Fixture_Output fixture_output_1: pin names not known; wires that end beside it: A, EA, Y
  // Fixture_Inout fixture_inout_1: pin names not known; wires that end beside it: B, EB, Y
endmodule
