// Logisim project arithmetic-components.circ as structural Verilog: 13 circuits, main circuit Adder
module Adder (
  output [7:0] result,
  output carryOut
);

  Adder_part #(.width(8)) adder_1 (.a(8'h3), .b(8'h2), .out(result), .cin(1'b1), .cout(carryOut));
endmodule

module Subtractor (
  output [7:0] result,
  output borrowOut
);

  Subtractor_part #(.width(8)) subtractor_1 (.a(8'h3), .b(8'h2), .out(result), .bin(1'b1), .bout(borrowOut));
endmodule

module Multiplier (
  output [7:0] low,
  output [7:0] high
);

  Multiplier_part #(.width(8)) multiplier_1 (.a(8'h3), .b(8'h2), .out(low), .cin(8'h1), .cout(high));
endmodule

module Divider (
  output [7:0] quotient,
  output [7:0] remainder
);

  Divider_part #(.width(8)) divider_1 (.a(8'h3), .b(8'h2), .out(quotient), .upper(8'h1), .rem(remainder));
endmodule

module Negator (
  output [7:0] result
);

  Negator_part #(.width(8)) negator_1 (.in(8'h3), .out(result));
endmodule

module Exponentiator (
  output [7:0] low,
  output [7:0] high
);

  // Exponentiator_part #(.width(8)) exponentiator_1: pin names not known; wires that end beside it: 8'h3, 8'h2, high, low
endmodule

module SquareRoot (
  output [7:0] root,
  output [7:0] remainder
);

  // SquareRoot_part #(.width(8)) squareroot_1: pin names not known; wires that end beside it: 8'h3, 8'h2, remainder, root
endmodule

module Absolute (
  output [7:0] result,
  output overflow
);

  // Absolute_part #(.width(8)) absolute_1: pin names not known; wires that end beside it: 8'hfd, overflow, result
endmodule

module Comparator (
  output greater,
  output equal,
  output less
);

  Comparator_part #(.width(8)) comparator_1 (.a(8'h3), .b(8'h2), .gt(greater), .eq(equal), .lt(less));
endmodule

module MinMax (
  output [7:0] minimum,
  output [7:0] maximum
);

  // MinMax_part #(.width(8)) minmax_1: pin names not known; wires that end beside it: 8'h3, 8'h2, minimum, maximum
endmodule

module Shifter (
  output [7:0] result
);

  Shifter_part #(.width(8)) shifter_1 (.in(8'h3), .\dist (3'b010), .out(result));
endmodule

module BitAdder (
  output [4:0] count
);

  BitAdder_part #(.width(8)) bitadder_1 (.in0(8'h3), .in1(8'h2), .out(count));
endmodule

module BitFinder (
  output [2:0] index,
  output present
);

  BitFinder_part #(.width(8)) bitfinder_1 (.in(8'h3), .index(index), .found(present));
endmodule
