// Logisim project ram-line-shared-bus.circ as structural Verilog: 1 circuit, main circuit main
module main (
  input  addr0,
  input  oe,
  input  addr1,
  input  we,
  input  addr2,
  input  le0,
  input  addr3,
  input  le1,
  input  le2,
  input  le3,
  output q0,
  output q1,
  output q2,
  output q3
);

  wire ram_1_p7;

  // RAM #(.addrWidth(4), .dataWidth(1), .enables("line"), .line("quad"), .databus("bidir"), .trigger("rising")) ram_1: pin names not known; wires that end beside it: oe, we, le0, le1, le2, le3, ram_1_p7, q0, q1, q2, q3
  Clock #(.highDuration(2), .lowDuration(3), .phaseOffset(0)) clock_1 (.out(ram_1_p7));
endmodule
