// Logisim project ram-mixed-line.circ as structural Verilog: 2 circuits, main circuit main
module main (
  input  a_addr0,
  input  a_addr1,
  input  a_we,
  input  a_din0,
  input  a_din1,
  input  b_addr0,
  input  b_addr1,
  input  b_we,
  input  b_clk,
  input  b_din0,
  input  b_din1,
  output a_q0,
  output a_q1,
  output b_q0,
  output b_q1
);

  wire clock_1_out;

  mem mem_1 (
    .addr0(a_addr0), .addr1(a_addr1), .we(a_we), .clk(clock_1_out), .din0(a_din0), .din1(a_din1), .q0(a_q0),
    .q1(a_q1));
  Clock #(.highDuration(2), .lowDuration(3), .phaseOffset(0)) clock_1 (.out(clock_1_out));
  mem mem_2 (
    .addr0(b_addr0), .addr1(b_addr1), .we(b_we), .clk(b_clk), .din0(b_din0), .din1(b_din1), .q0(b_q0),
    .q1(b_q1));
endmodule

module mem (
  input  addr0,
  input  addr1,
  input  we,
  input  clk,
  input  din0,
  input  din1,
  output q0,
  output q1
);

  RAM #(.addrWidth(2), .dataWidth(2), .enables("line"), .databus("bibus"), .trigger("rising"), .line("single")) ram_1 (
    .addr({addr1, addr0}), .we(we), .clk(clk), .din({din1, din0}), .dout({q1, q0}));
endmodule
