// Logisim project reptar-clock.circ as structural Verilog: 1 circuit, main circuit main
module main (
);

  wire LocalBus_p2, tick_out;

  Clock #(.highDuration(1), .lowDuration(1), .phaseOffset(0)) tick (.out(tick_out));
  // ReptarLB LocalBus: pin names not known; wires that end beside it: 16'h3456, LocalBus_p2
  T_Flip_Flop #(.trigger("rising")) t_ff_1 (.clk(tick_out), .T(1'b1), .Q(LocalBus_p2));  // open: Qn, preset, reset
endmodule
