// Logisim project sr-dedicated.circ as structural Verilog: 1 circuit, main circuit main
module main (
  input  set_in,
  input  reset_in,
  output q_out
);

  wire clock_1_out;

  Clock #(.highDuration(2), .lowDuration(3)) clock_1 (.out(clock_1_out));
  S_R_Flip_Flop #(.trigger("rising")) s_r_ff_1 (
    .S(set_in), .clk(clock_1_out), .R(reset_in), .Q(q_out), .preset(1'b0), .reset(1'b0));  // open: Qn
endmodule
