// Logisim project terminal-echo-271.circ as structural Verilog: 1 circuit, main circuit main
module main (
);

  wire clock_1_out, keyboard_1_avail;
  wire [6:0] keyboard_1_data;

  Clock clock_1 (.out(clock_1_out));
  Keyboard #(.trigger("falling"), .buflen(2)) keyboard_1 (
    .clk(clock_1_out), .re(keyboard_1_avail), .avail(keyboard_1_avail), .data(keyboard_1_data));  // open: clr
  TTY #(.trigger("falling"), .cols(2)) tty_1 (
    .data(keyboard_1_data), .clk(clock_1_out), .we(keyboard_1_avail));  // open: clr
endmodule
