// Logisim project tristate-271.circ as structural Verilog: 1 circuit, main circuit main
module main (
  input  EN,
  output Y
);

  assign Y = EN ? 1'b1 : 1'bz;  // Controlled_Buffer controlled_buffer_1
endmodule
