// Logisim project inverter.circ as structural Verilog: 1 circuit, main circuit main
module main (
  input  [3:0] A,
  output [3:0] Y
);

  // Bus_Inverter bus_inverter_1: pin names not known; wires that end beside it: A, Y
endmodule
