// Logisim project original-and-default-inputs.circ as structural Verilog: 1 circuit, main circuit main
module main (
  output Y,
  output halt
);

  and and_1 (Y, 1'b1, 1'b0, 1'b1);

  assign halt = 1'b1;
endmodule
