// Logisim project mux-disabled.circ as structural Verilog: 1 circuit, main circuit main
module main (
  output Y,
  output halt
);

  Multiplexer multiplexer_1 (.in0(1'b1), .in1(1'b0), .out(Y), .sel(1'b0), .en(1'b0));

  assign halt = 1'b1;
endmodule
