// Logisim project plexers-disabled.circ as structural Verilog: 1 circuit, main circuit main
module main (
  output out_1,
  output out_2,
  output [2:0] out_3
);

  Priority_Encoder priority_encoder_1 (
    .out(out_3), .en_in(1'b0));  // open: in0, in1, in2, in3, in4, in5, in6, in7, gs, en_out
  Demultiplexer demultiplexer_1 (.out0(out_2), .en(1'b0));  // open: out1, in, sel
  Decoder decoder_1 (.out0(out_1), .en(1'b0));  // open: out1, sel
endmodule
