// Logisim project counter.circ as structural Verilog: 1 circuit, main circuit main
module main (
  output [3:0] Q,
  output halt
);

  Counter #(.width(4), .max('hf)) counter_1 (
    .load(1'b1), .D(4'b0101), .count(1'b1), .Q(Q), .clk(halt));  // open: carry, up, clr
  Clock clock_1 (.out(halt));
endmodule
