// Logisim project gate-undefined-default.circ as structural Verilog: 1 circuit, main circuit main
module main (
  input  a0,
  input  a1,
  input  a2,
  input  b2,
  input  a3,
  input  a6,
  input  a8,
  input  a9,
  input  c9,
  output y0_and_open,
  output y1_or_stub,
  output y2_and_driven,
  output y3_xor_stub,
  output y4_nand_none,
  output y5_not_stub,
  output y6_not_driven,
  output y7_buffer_stub,
  output y8_cbuf_open,
  output y9_cbuf_driven
);

  wire undriven, undriven_2, undriven_3, xor_1_p1;

  buf and_1 (y0_and_open, a0);  // AND_Gate
  or or_1 (y1_or_stub, a1, undriven);
  and and_2 (y2_and_driven, a2, b2);
  // XOR_Gate xor_1: pin names not known; wires that end beside it: xor_1_p1, a3, xor_1_p1, y3_xor_stub
  // NAND_Gate nand_1 has open pins: out=y4_nand_none
  not not_1 (y5_not_stub, undriven_2);
  not not_2 (y6_not_driven, a6);
  buf buffer_1 (y7_buffer_stub, undriven_3);
  Controlled_Buffer controlled_buffer_1 (.in(a8), .out(y8_cbuf_open));  // open: en
  assign y9_cbuf_driven = c9 ? a9 : 1'bz;  // Controlled_Buffer controlled_buffer_2
endmodule
