// Logisim project simrand-race-32.circ as structural Verilog: 1 circuit, main circuit main
module main (
  output halt
);

  wire and_1_out, buffer_1_out, clock_1_out, nor_1_p3, not_1_out;

  Clock clock_1 (.out(clock_1_out));
  not not_1 (not_1_out, clock_1_out);
  buf buffer_1 (buffer_1_out, clock_1_out);
  and and_1 (and_1_out, not_1_out, buffer_1_out);
  // NOR_Gate nor_1: pin names not known; wires that end beside it: and_1_out, halt, nor_1_p3
  // NOR_Gate nor_2: pin names not known; wires that end beside it: nor_1_p3, halt
endmodule
