// Logisim project simrand-network-32.circ as structural Verilog: 1 circuit, main circuit main
module main (
  input  a,
  input  b,
  input  c,
  output x,
  output y
);

  wire and_1_out;

  // XOR_Gate xor_1: pin names not known; wires that end beside it: a, b, x
  and and_1 (and_1_out, x, c);
  or or_1 (y, and_1_out, x);
endmodule
