// Logisim project exported.circ as structural Verilog: 1 circuit, main circuit AND
module AND (
  input  A,
  input  B,
  output A_AND_B
);

  and and_1 (A_AND_B, A, B);

  // Notes on the sheet:
  //   A: initial=0
  //   B: initial=0
endmodule
