// Logisim project exported.circ as structural Verilog: 2 circuits, main circuit Hierarchy
module Hierarchy (
  input  A,
  output Y
);

  Inversor inversor_1 (.Entrada(A), .\Saída (Y));
endmodule

module Inversor (
  input  Entrada,
  output \Saída 
);

  not not_1 (\Saída , Entrada);
endmodule
