// Logisim project exported.circ as structural Verilog: 1 circuit, main circuit RomLookup
module RomLookup (
  input  [1:0] ADDR,
  output [7:0] Dados
);

  ROM #(.addrWidth(2), .dataWidth(8)) rom_1 (.addr(ADDR), .data(Dados));

  // Notes on the sheet:
  //   contents of rom_1 (hex, n*v repeats v):
  //   12 34 56 78
endmodule
