// Logisim project editing-property-redo.circ as structural Verilog: 1 circuit, main circuit Sem título
module \Sem_título  (
  input  E2E_IN,
  output E2E_OUT
);

  // NOT_Gate E2E_NOT is placed but not wired
endmodule
