// Logisim project failure-checkpoint-23.circ as structural Verilog: 1 circuit, main circuit Sem título
module \Sem_título  (
  input  E2E_IN
);

  // NOT_Gate not_1 is placed but not wired
endmodule
