// Logisim project editing-create-properties-checkpoint-28.circ as structural Verilog: 1 circuit, main circuit Sem título
module \Sem_título  (
  input  E2E_IN,
  output out_2
);

  // NOT_Gate E2E_NOT is placed but not wired
endmodule
