// Logisim project editing-pasted.circ as structural Verilog: 1 circuit, main circuit Sem título
module \Sem_título  (
  input  E2E_IN,
  input  E2E_IN_2,
  output E2E_OUT,
  output E2E_OUT_2
);

  not E2E_NOT (E2E_OUT, E2E_IN);
  not E2E_NOT_2 (E2E_OUT_2, E2E_IN_2);
endmodule
