// Logisim project editing-touch-or.circ as structural Verilog: 1 circuit, main circuit Sem título
module \Sem_título  (
  input  E2E_IN,
  output E2E_OUT
);

  not E2E_NOT (E2E_OUT, E2E_IN);
  // OR_Gate or_1 is placed but not wired
endmodule
