// Logisim project editing-wire-removed.circ as structural Verilog: 1 circuit, main circuit Sem título
module \Sem_título  (
  input  E2E_IN,
  output E2E_OUT
);

  // NOT_Gate E2E_NOT has open pins: in=open, out=E2E_OUT
endmodule
