// Logisim project 0-fixture.circ as structural Verilog: 1 circuit, main circuit io-release_deeb6aa5
module io_release_deeb6aa5 (
  output MI_io_release_deeb6aa5_OUT
);

  Button MI_io_release_deeb6aa5_BUTTON (.out(MI_io_release_deeb6aa5_OUT));
endmodule
