// Logisim project 0-fixture.circ as structural Verilog: 1 circuit, main circuit pinch_23376e84
module pinch_23376e84 (
  input  MI_pinch_23376e84_IN,
  output MI_pinch_23376e84_OUT
);

  not MI_pinch_23376e84_NOT (MI_pinch_23376e84_OUT, MI_pinch_23376e84_IN);
endmodule
