// Logisim project 3-cancel-valid-move.circ as structural Verilog: 1 circuit, main circuit cancel_9a8f578f
module cancel_9a8f578f (
  input  MI_cancel_9a8f578f_IN,
  output MI_cancel_9a8f578f_OUT
);

  not MI_cancel_9a8f578f_NOT (MI_cancel_9a8f578f_OUT, MI_cancel_9a8f578f_IN);
endmodule
