// Logisim project 1-context-before.circ as structural Verilog: 1 circuit, main circuit context_ac0931ca
module context_ac0931ca (
  input  MI_context_ac0931ca_IN,
  output MI_context_ac0931ca_OUT
);

  not MI_context_ac0931ca_NOT (MI_context_ac0931ca_OUT, MI_context_ac0931ca_IN);
endmodule
