// Logisim project 2-context-duplicate.circ as structural Verilog: 1 circuit, main circuit context_ac0931ca
module context_ac0931ca (
  input  MI_context_ac0931ca_IN,
  output MI_context_ac0931ca_OUT
);

  not MI_context_ac0931ca_NOT (MI_context_ac0931ca_OUT, MI_context_ac0931ca_IN);
  // NOT_Gate MI_context_ac0931ca_NOT_2 is placed but not wired
endmodule
