// Logisim project 3-cancel-valid-move.circ as structural Verilog: 1 circuit, main circuit cancel_1b30597a
module cancel_1b30597a (
  input  MI_cancel_1b30597a_IN,
  output MI_cancel_1b30597a_OUT
);

  not MI_cancel_1b30597a_NOT (MI_cancel_1b30597a_OUT, MI_cancel_1b30597a_IN);
endmodule
