// Logisim project 0-fixture.circ as structural Verilog: 1 circuit, main circuit context_b903be92
module context_b903be92 (
  input  MI_context_b903be92_IN,
  output MI_context_b903be92_OUT
);

  not MI_context_b903be92_NOT (MI_context_b903be92_OUT, MI_context_b903be92_IN);
endmodule
