// Logisim project 5-mixed-keyboard-undo.circ as structural Verilog: 1 circuit, main circuit mixed_02d7a544
module mixed_02d7a544 (
  input  MI_mixed_02d7a544_IN,
  output MI_mixed_02d7a544_OUT
);

  not MI_mixed_02d7a544_NOT (MI_mixed_02d7a544_OUT, MI_mixed_02d7a544_IN);
endmodule
