// Logisim project 0-fixture.circ as structural Verilog: 1 circuit, main circuit focusloss_0e889039
module focusloss_0e889039 (
  input  MI_focusloss_0e889039_IN,
  output MI_focusloss_0e889039_OUT
);

  not MI_focusloss_0e889039_NOT (MI_focusloss_0e889039_OUT, MI_focusloss_0e889039_IN);
endmodule
