// Logisim project 1-focusloss-before.circ as structural Verilog: 1 circuit, main circuit focusloss_b71abad7
module focusloss_b71abad7 (
  input  MI_focusloss_b71abad7_IN,
  output MI_focusloss_b71abad7_OUT
);

  not MI_focusloss_b71abad7_NOT (MI_focusloss_b71abad7_OUT, MI_focusloss_b71abad7_IN);
endmodule
