// Logisim project staged-external.circ as structural Verilog: 1 circuit, main circuit IOS-E2E-c702d6c5c277-external
module IOS_E2E_c702d6c5c277_external (
  input  E2E_IN,
  output E2E_OUT
);

  not E2E_NOT (E2E_OUT, E2E_IN);
endmodule
