// Logisim project 0-fixture.circ as structural Verilog: 1 circuit, main circuit pinch_54f93399
module pinch_54f93399 (
  input  MI_pinch_54f93399_IN,
  output MI_pinch_54f93399_OUT
);

  not MI_pinch_54f93399_NOT (MI_pinch_54f93399_OUT, MI_pinch_54f93399_IN);
endmodule
