// Logisim project fpga-synthesis-checkpoint-10.circ as structural Verilog: 1 circuit, main circuit layout12
module layout12 (
  input  Reset
);

  // Image #(.image("data:image/png;base64,iVBORw0KGgoAAAANSUhEUgAAAAEAAAABCAYAAAAfFcSJAAAADUlEQVR4nGN4oLDgPwAGJAKg3WwsdQAAAABJRU5ErkJggg=="), .width(32), .height(24), .scale("stretch"), .license("CC0-1.0"), .attribution("Synthetic single-color pixel for layout qualification")) image_1: pin names not known
  // Image #(.image("data:image/png;base64,iVBORw0KGgoAAAANSUhEUgAAAAEAAAABCAYAAAAfFcSJAAAADUlEQVR4nGMQ2HDhPwAE9AKQia+IqAAAAABJRU5ErkJggg=="), .width(40), .height(32), .scale("stretch"), .license("CC0-1.0"), .attribution("Synthetic single-color pixel for layout qualification")) image_2: pin names not known; wires that end beside it: Reset
endmodule
