// Logisim project fpga-failure-checkpoint-52.circ as structural Verilog: 1 circuit, main circuit External_IO61
module External_IO61 (
  input  EXT61_IN_VIDEO_RESET,
  input  EXT61_IN_VIDEO_CLOCK,
  input  [7:0] EXT61_IN_TELNET_DATA,
  input  EXT61_IN_TELNET_CLOCK,
  input  EXT61_IN_TELNET_WRITE,
  input  EXT61_IN_VIDEO_WRITE,
  input  EXT61_IN_TELNET_READ,
  input  [1:0] EXT61_IN_VIDEO_X,
  input  [1:0] EXT61_IN_VIDEO_Y,
  input  [23:0] EXT61_IN_VIDEO_DATA,
  output [3:0] EXT61_OUT_PORT_IO,
  output [63:0] EXT61_OUT_RTC,
  output EXT61_OUT_VIDEO_CLOCK,
  output [7:0] EXT61_OUT_TELNET_DATA,
  output EXT61_OUT_TELNET_AVAILABLE,
  output [23:0] EXT61_OUT_VIDEO_DATA
);

  // PortIO #(.mapinfo("native61-preserve:EXT61_PORT_IO"), .number(4), .direction("onlyinput")) EXT61_PORT_IO: pin names not known; wires that end beside it: EXT61_OUT_PORT_IO
  // ReptarLB #(.mapinfo("native61-preserve:EXT61_REPTAR")) EXT61_REPTAR: pin names not known
  // Telnet #(.mapinfo("native61-preserve:EXT61_TELNET"), .port(8000), .buflen(8), .trigger("rising"), .telnetMode("false")) EXT61_TELNET: pin names not known; wires that end beside it: EXT61_IN_TELNET_DATA, EXT61_IN_TELNET_CLOCK, EXT61_IN_TELNET_WRITE, EXT61_OUT_TELNET_DATA, EXT61_OUT_TELNET_AVAILABLE, EXT61_IN_TELNET_READ
  // RealTimeClock #(.mapinfo("native61-preserve:EXT61_RTC"), .timeType(2), .porsize(1)) EXT61_RTC: pin names not known; wires that end beside it: EXT61_OUT_RTC
  // RGB_Video #(.mapinfo("native61-preserve:EXT61_VIDEO"), .width(4), .height(3), .scale(8), .reset("Asynchronous"), .cursor("No Cursor")) EXT61_VIDEO: pin names not known; wires that end beside it: EXT61_IN_VIDEO_RESET, EXT61_IN_VIDEO_CLOCK, EXT61_IN_VIDEO_WRITE, EXT61_IN_VIDEO_X, EXT61_IN_VIDEO_Y, EXT61_IN_VIDEO_DATA

  assign EXT61_OUT_VIDEO_CLOCK = EXT61_IN_VIDEO_CLOCK;
  assign EXT61_OUT_VIDEO_DATA = EXT61_IN_VIDEO_DATA;

  // Notes on the sheet:
  //   EXT61_IN_VIDEO_RESET: initial=0
  //   EXT61_IN_VIDEO_CLOCK: initial=0
  //   EXT61_IN_VIDEO_WRITE: initial=0
  //   EXT61_IN_VIDEO_X: initial=1
  //   EXT61_IN_VIDEO_Y: initial=1
  //   EXT61_IN_VIDEO_DATA: initial=1223629
  //   EXT61_IN_TELNET_DATA: initial=65
  //   EXT61_IN_TELNET_CLOCK: initial=0
  //   EXT61_IN_TELNET_WRITE: initial=0
  //   EXT61_IN_TELNET_READ: initial=0
endmodule
