// Logisim project fpga-failure-checkpoint-73.circ as structural Verilog: 1 circuit, main circuit pinch_80ac7783
module pinch_80ac7783 (
  input  MI_pinch_80ac7783_IN,
  output MI_pinch_80ac7783_OUT
);

  not MI_pinch_80ac7783_NOT (MI_pinch_80ac7783_OUT, MI_pinch_80ac7783_IN);
endmodule
