// Logisim project fpga-synthesis-checkpoint-21.circ as structural Verilog: 1 circuit, main circuit focus_f1f7200c
module focus_f1f7200c (
  input  MI_focus_f1f7200c_IN,
  output MI_focus_f1f7200c_OUT
);

  not not_1 (MI_focus_f1f7200c_OUT, MI_focus_f1f7200c_IN);
endmodule
