// Logisim project fpga-synthesis-checkpoint-91.circ as structural Verilog: 1 circuit, main circuit scroll_1220a87c
module scroll_1220a87c (
  input  MI_scroll_1220a87c_IN,
  output MI_scroll_1220a87c_OUT
);

  not MI_scroll_1220a87c_NOT (MI_scroll_1220a87c_OUT, MI_scroll_1220a87c_IN);
endmodule
