// Logisim project fpga-failure-checkpoint-3.circ as structural Verilog: 1 circuit, main circuit Minha primeira porta AND
module Minha_primeira_porta_AND (
  input  A,
  input  B,
  output \Saída 
);

  and AND (\Saída , A, B);
endmodule
