// Logisim project io-dimension-io_dot_matrix-matrixrows.circ as structural Verilog: 1 circuit, main circuit IO_Showcase
module IO_Showcase (
  input  IN_RGB_G,
  input  IN_RGB_R,
  input  IN_RGB_B,
  input  IN_LED_LEVEL,
  input  [7:0] IN_BAR_VALUE,
  input  [7:0] IN_SEGMENTS,
  input  [4:0] IN_MATRIX_ROW_0,
  input  IN_READ_ENABLE,
  input  IN_KEYBOARD_CLEAR,
  input  [4:0] IN_MATRIX_ROW_1,
  input  [4:0] IN_MATRIX_ROW_2,
  input  [4:0] IN_MATRIX_ROW_3,
  input  [4:0] IN_MATRIX_ROW_4,
  input  [4:0] IN_MATRIX_ROW_5,
  input  [4:0] IN_MATRIX_ROW_6,
  input  IN_WRITE_ENABLE,
  input  IN_TTY_CLEAR,
  input  IN_SCAN_ROW_0,
  input  IN_SCAN_ROW_1,
  input  IN_SCAN_ROW_2,
  input  IN_SCAN_ROW_3,
  output OUT_RGB_G,
  output OUT_RGB_R,
  output OUT_BUTTON,
  output OUT_LED_LEVEL,
  output OUT_RGB_B,
  output [7:0] OUT_BAR_VALUE,
  output OUT_DIP0,
  output [3:0] OUT_JOY_X,
  output OUT_DIP1,
  output [7:0] OUT_SEGMENTS,
  output [3:0] OUT_JOY_Y,
  output [4:0] OUT_MATRIX_ROW0,
  output [6:0] OUT_KEYBOARD_DATA,
  output OUT_KEYBOARD_AVAILABLE,
  output OUT_CLOCK,
  output OUT_KEYPAD_C0,
  output OUT_KEYPAD_C1,
  output OUT_KEYPAD_C2,
  output OUT_KEYPAD_C3
);

  // DipSwitch #(.number(8), .resetbehavior("last"), .positions(0)) IO_DIP: pin names not known; wires that end beside it: OUT_DIP0, OUT_DIP1
  Clock #(.highDuration(1), .lowDuration(1), .phaseOffset(0)) IO_CLOCK (.out(OUT_CLOCK));
  Button #(.press("active")) IO_BUTTON (.out(OUT_BUTTON));
  Keyboard #(.buflen(16), .trigger("rising")) IO_KEYBOARD (
    .clk(OUT_CLOCK), .re(IN_READ_ENABLE), .clr(IN_KEYBOARD_CLEAR), .avail(OUT_KEYBOARD_AVAILABLE),
    .data(OUT_KEYBOARD_DATA));
  // MatrixKeypad #(.mode("pmod_kypd")) IO_KEYPAD: pin names not known; wires that end beside it: IN_SCAN_ROW_0, IN_SCAN_ROW_1, IN_SCAN_ROW_2, IN_SCAN_ROW_3, OUT_KEYPAD_C0, OUT_KEYPAD_C1, OUT_KEYPAD_C2, OUT_KEYPAD_C3
  LED #(.active("true")) IO_LED_BUTTON (.in(OUT_BUTTON));
  Joystick #(.bits(4)) IO_JOYSTICK (.x(OUT_JOY_X), .y(OUT_JOY_Y));
  TTY #(.rows(3), .cols(12), .trigger("rising")) IO_TTY (
    .data(OUT_KEYBOARD_DATA), .clk(OUT_CLOCK), .we(IN_WRITE_ENABLE), .clr(IN_TTY_CLEAR));
  LED #(.active("true")) IO_LED (.in(IN_LED_LEVEL));
  Hex_Digit_Display #(.decimalPoint("false")) IO_HEX (.value(OUT_JOY_X));
  // RGBLED #(.active("true")) IO_RGB: pin names not known; wires that end beside it: IN_RGB_R, IN_RGB_G, IN_RGB_B
  // LedBar #(.inputtype("row"), .matrixcols(8), .matrixrows(1), .height(3)) IO_LEDBAR: pin names not known; wires that end beside it: IN_SEGMENTS, IN_BAR_VALUE
  _7_Segment_Display #(.inputmode("bus"), .decimalPoint("true"), .busside("west")) IO_SEVEN_SEGMENT ();  // open: g, f, a, b, e, d, c, dp
  DotMatrix #(.inputtype("row"), .matrixrows(8), .matrixcols(5), .persist(0), .dotshape("square")) IO_DOT_MATRIX (
    .row0(IN_MATRIX_ROW_0), .row1(IN_MATRIX_ROW_1), .row2(IN_MATRIX_ROW_2), .row3(IN_MATRIX_ROW_3),
    .row4(IN_MATRIX_ROW_4), .row5(IN_MATRIX_ROW_5), .row6(IN_MATRIX_ROW_6));  // open: row7

  assign OUT_BAR_VALUE = IN_BAR_VALUE;
  assign OUT_LED_LEVEL = IN_LED_LEVEL;
  assign OUT_MATRIX_ROW0 = IN_MATRIX_ROW_0;
  assign OUT_RGB_B = IN_RGB_B;
  assign OUT_RGB_G = IN_RGB_G;
  assign OUT_RGB_R = IN_RGB_R;
  assign OUT_SEGMENTS = IN_SEGMENTS;

  // Notes on the sheet:
  //   IN_LED_LEVEL: initial=0
  //   IN_RGB_R: initial=1
  //   IN_RGB_G: initial=1
  //   IN_RGB_B: initial=0
  //   IN_BAR_VALUE: initial=165
  //   IN_SEGMENTS: initial=63
  //   IN_READ_ENABLE: initial=1
  //   IN_KEYBOARD_CLEAR: initial=0
  //   IN_WRITE_ENABLE: initial=1
  //   IN_TTY_CLEAR: initial=0
  //   IN_MATRIX_ROW_0: initial=14
  //   IN_MATRIX_ROW_1: initial=17
  //   IN_MATRIX_ROW_2: initial=17
  //   IN_MATRIX_ROW_3: initial=31
  //   IN_MATRIX_ROW_4: initial=17
  //   IN_MATRIX_ROW_5: initial=17
  //   IN_MATRIX_ROW_6: initial=17
  //   IN_SCAN_ROW_0: initial=0
  //   IN_SCAN_ROW_1: initial=1
  //   IN_SCAN_ROW_2: initial=1
  //   IN_SCAN_ROW_3: initial=1
endmodule
