// Logisim project external.circ as structural Verilog: 1 circuit, main circuit IOS-E2E-e20987fdc1cc-external
module IOS_E2E_e20987fdc1cc_external (
  input  E2E_IN,
  output E2E_OUT
);

  not E2E_NOT (E2E_OUT, E2E_IN);
endmodule
