// Logisim project bridge.circ as structural Verilog: 1 circuit, main circuit Bridge53
module Bridge53 (
  input  [7:0] BRIDGE_IN53,
  output [7:0] BRIDGE_OUT53
);

  Cell53 TRANSITIVE53 (.CELL_IN53(BRIDGE_IN53), .CELL_OUT53(BRIDGE_OUT53));
endmodule
