// Logisim project backend-after.circ as structural Verilog: 1 circuit, main circuit provider_revocation
module provider_revocation (
  input  REVOCATION_INPUT,
  output REVOCATION_OUTPUT
);


  assign REVOCATION_OUTPUT = REVOCATION_INPUT;
endmodule
