// Logisim project peer-copy-baseline.circ as structural Verilog: 1 circuit, main circuit IOS-PEER-5f364710641a
module IOS_PEER_5f364710641a (
  input  E2E_IN,
  output E2E_OUT
);

  not E2E_NOT (E2E_OUT, E2E_IN);
endmodule
