// Logisim project peer-restored-after-restart.circ as structural Verilog: 1 circuit, main circuit IOS-PEER-5f364710641a
module IOS_PEER_5f364710641a (
  input  PEER_EDIT_5f364710641a,
  output E2E_OUT
);

  not E2E_NOT (E2E_OUT, PEER_EDIT_5f364710641a);
endmodule
