// Logisim project portable-bundle-reopened.circ as structural Verilog: 3 circuits, main circuit Top53
module Top53 (
  output [7:0] OUT_FIRST53,
  output [7:0] OUT_SECOND53
);

  library_4c2deaef278e2ab4_Bridge53 FIRST53 (.BRIDGE_IN53(8'h8), .BRIDGE_OUT53(OUT_FIRST53));
  library_4c2deaef278e2ab4_Bridge53 SECOND53 (.BRIDGE_IN53(8'h3), .BRIDGE_OUT53(OUT_SECOND53));
endmodule

module library_c4304ec01994bf4c_Cell53 (
  input  [7:0] CELL_IN53,
  output [7:0] CELL_OUT53
);


  assign CELL_OUT53 = CELL_IN53;
endmodule

module library_4c2deaef278e2ab4_Bridge53 (
  input  [7:0] BRIDGE_IN53,
  output [7:0] BRIDGE_OUT53
);

  library_c4304ec01994bf4c_Cell53 TRANSITIVE53 (.CELL_IN53(BRIDGE_IN53), .CELL_OUT53(BRIDGE_OUT53));
endmodule
