// Logisim project cold.circ as structural Verilog: 1 circuit, main circuit IOS-E2E-a019f18cae2d-cold
module IOS_E2E_a019f18cae2d_cold (
  input  E2E_IN,
  output E2E_OUT
);

  not E2E_NOT (E2E_OUT, E2E_IN);
endmodule
