// Logisim project peer.circ as structural Verilog: 1 circuit, main circuit IOS-PEER-a019f18cae2d
module IOS_PEER_a019f18cae2d (
  input  E2E_IN,
  output E2E_OUT
);

  not E2E_NOT (E2E_OUT, E2E_IN);
endmodule
