// Logisim project io-held-output.circ as structural Verilog: 1 circuit, main circuit IO_Held_Output
module IO_Held_Output (
  output OUT_HELD,
  output REF_LOW,
  output REF_HIGH
);

  Button #(.press("active")) BTN_HELD (.out(OUT_HELD));

  assign REF_HIGH = 1'b1;
  assign REF_LOW = 1'b0;
endmodule
