// Logisim project visual-export-3b6fa3c060c7.circ as structural Verilog: 3 circuits, main circuit visual_export_qualification
module visual_export_qualification (
);

  // Image #(.image("data:image/png;base64,iVBORw0KGgoAAAANSUhEUgAAAAIAAAABCAYAAAD0In+KAAAAD0lEQVR4nGP4z8DwHwgbABB5A359Y87XAAAAAElFTkSuQmCC"), .width(120), .height(80), .scale("cover"), .attribution("Author & source")) EXPORT34_IMAGE: pin names not known
  child child_1 ();  // open: A, Y
  child child_2 ();  // open: A, Y
  child EXPORT34_CELL_000 ();  // open: A, Y
  child EXPORT34_CELL_012 ();  // open: A, Y
  child EXPORT34_CELL_024 ();  // open: A, Y
  child EXPORT34_CELL_036 ();  // open: A, Y
  child EXPORT34_CELL_048 ();  // open: A, Y
  child EXPORT34_CELL_060 ();  // open: A, Y
  classicChild classicchild_1 ();  // open: A, Y
  child EXPORT34_CELL_001 ();  // open: A, Y
  child EXPORT34_CELL_013 ();  // open: A, Y
  child EXPORT34_CELL_025 ();  // open: A, Y
  child EXPORT34_CELL_037 ();  // open: A, Y
  child EXPORT34_CELL_049 ();  // open: A, Y
  child EXPORT34_CELL_061 ();  // open: A, Y
  child EXPORT34_CELL_002 ();  // open: A, Y
  child EXPORT34_CELL_014 ();  // open: A, Y
  child EXPORT34_CELL_026 ();  // open: A, Y
  child EXPORT34_CELL_038 ();  // open: A, Y
  child EXPORT34_CELL_050 ();  // open: A, Y
  child EXPORT34_CELL_062 ();  // open: A, Y
  child EXPORT34_CELL_003 ();  // open: A, Y
  child EXPORT34_CELL_015 ();  // open: A, Y
  child EXPORT34_CELL_027 ();  // open: A, Y
  child EXPORT34_CELL_039 ();  // open: A, Y
  child EXPORT34_CELL_051 ();  // open: A, Y
  child EXPORT34_CELL_063 ();  // open: A, Y
  child EXPORT34_CELL_004 ();  // open: A, Y
  child EXPORT34_CELL_016 ();  // open: A, Y
  child EXPORT34_CELL_028 ();  // open: A, Y
  child EXPORT34_CELL_040 ();  // open: A, Y
  child EXPORT34_CELL_052 ();  // open: A, Y
  child EXPORT34_CELL_064 ();  // open: A, Y
  child EXPORT34_CELL_005 ();  // open: A, Y
  child EXPORT34_CELL_017 ();  // open: A, Y
  child EXPORT34_CELL_029 ();  // open: A, Y
  child EXPORT34_CELL_041 ();  // open: A, Y
  child EXPORT34_CELL_053 ();  // open: A, Y
  child EXPORT34_CELL_065 ();  // open: A, Y
  child EXPORT34_CELL_006 ();  // open: A, Y
  child EXPORT34_CELL_018 ();  // open: A, Y
  child EXPORT34_CELL_030 ();  // open: A, Y
  child EXPORT34_CELL_042 ();  // open: A, Y
  child EXPORT34_CELL_054 ();  // open: A, Y
  child EXPORT34_CELL_066 ();  // open: A, Y
  child EXPORT34_CELL_007 ();  // open: A, Y
  child EXPORT34_CELL_019 ();  // open: A, Y
  child EXPORT34_CELL_031 ();  // open: A, Y
  child EXPORT34_CELL_043 ();  // open: A, Y
  child EXPORT34_CELL_055 ();  // open: A, Y
  child EXPORT34_CELL_067 ();  // open: A, Y
  child EXPORT34_CELL_008 ();  // open: A, Y
  child EXPORT34_CELL_020 ();  // open: A, Y
  child EXPORT34_CELL_032 ();  // open: A, Y
  child EXPORT34_CELL_044 ();  // open: A, Y
  child EXPORT34_CELL_056 ();  // open: A, Y
  child EXPORT34_CELL_068 ();  // open: A, Y
  child EXPORT34_CELL_009 ();  // open: A, Y
  child EXPORT34_CELL_021 ();  // open: A, Y
  child EXPORT34_CELL_033 ();  // open: A, Y
  child EXPORT34_CELL_045 ();  // open: A, Y
  child EXPORT34_CELL_057 ();  // open: A, Y
  child EXPORT34_CELL_069 ();  // open: A, Y
  child EXPORT34_CELL_010 ();  // open: A, Y
  child EXPORT34_CELL_022 ();  // open: A, Y
  child EXPORT34_CELL_034 ();  // open: A, Y
  child EXPORT34_CELL_046 ();  // open: A, Y
  child EXPORT34_CELL_058 ();  // open: A, Y
  child EXPORT34_CELL_070 ();  // open: A, Y
  child EXPORT34_CELL_011 ();  // open: A, Y
  child EXPORT34_CELL_023 ();  // open: A, Y
  child EXPORT34_CELL_035 ();  // open: A, Y
  child EXPORT34_CELL_047 ();  // open: A, Y
  child EXPORT34_CELL_059 ();  // open: A, Y
  child EXPORT34_CELL_071 ();  // open: A, Y

  // Notes on the sheet:
  //     A & B
  //   linha  
  //   EXPORT34_FAR
endmodule

module child (
  input  [7:0] A,
  output [7:0] Y
);
endmodule

module classicChild (
  input  [7:0] A,
  output [7:0] Y
);
endmodule
