// Logisim project warm.circ as structural Verilog: 1 circuit, main circuit IOS-E2E-3b6fa3c060c7-warm
module IOS_E2E_3b6fa3c060c7_warm (
  input  E2E_IN,
  output E2E_OUT
);

  not E2E_NOT (E2E_OUT, E2E_IN);
endmodule
