// Logisim project control.circ as structural Verilog: 1 circuit, main circuit IOS-PEER-3b6fa3c060c7
module IOS_PEER_3b6fa3c060c7 (
  input  E2E_IN,
  output E2E_OUT
);

  not E2E_NOT (E2E_OUT, E2E_IN);
endmodule
