// Logisim project cold.circ as structural Verilog: 1 circuit, main circuit IOS-E2E-44c9bdc751d1-cold
module IOS_E2E_44c9bdc751d1_cold (
  input  E2E_IN,
  output E2E_OUT
);

  not E2E_NOT (E2E_OUT, E2E_IN);
endmodule
