// Logisim project warm.circ as structural Verilog: 1 circuit, main circuit IOS-E2E-467909817417-warm
module IOS_E2E_467909817417_warm (
  input  E2E_IN,
  output E2E_OUT
);

  not E2E_NOT (E2E_OUT, E2E_IN);
endmodule
