// Logisim project main.circ as structural Verilog: 1 circuit, main circuit Top53
module Top53 (
  output [7:0] OUT_FIRST53,
  output [7:0] OUT_SECOND53
);

  Bridge53 FIRST53 (.BRIDGE_IN53(8'h8), .BRIDGE_OUT53(OUT_FIRST53));
  Bridge53 SECOND53 (.BRIDGE_IN53(8'h3), .BRIDGE_OUT53(OUT_SECOND53));
endmodule
