// Logisim project bus-adder.circ as structural Verilog: 1 circuit, main circuit BusAdder
module BusAdder (
  input  [7:0] A,
  input  [7:0] B,
  output [7:0] S,
  output Carry
);

  Adder #(.width(8)) adder_1 (.a(A), .b(B), .out(S), .cout(Carry));  // open: cin
endmodule
