// Logisim project annotations-symbols.circ as structural Verilog: 3 circuits, main circuit main
module main (
);

  // Image #(.image("data:image/png;base64,iVBORw0KGgoAAAANSUhEUgAAAAIAAAABCAYAAAD0In+KAAAAD0lEQVR4nGP4z8DwHwgbABB5A359Y87XAAAAAElFTkSuQmCC"), .width(120), .height(80), .scale("cover"), .attribution("Author & source"), .mobile_group("group-1")) image_1: pin names not known
  child child_1 ();  // open: A, Y
  child child_2 ();  // open: A, Y
  classicChild classicchild_1 ();  // open: A, Y

  // Notes on the sheet:
  //     A & B
  //   linha  
endmodule

module child (
  input  [7:0] A,
  output [7:0] Y
);
endmodule

module classicChild (
  input  [7:0] A,
  output [7:0] Y
);
endmodule
