// Logisim project appearance-default-text.circ as structural Verilog: 2 circuits, main circuit top
module top (
);

  child child_1 ();  // open: input, out_2
endmodule

module child (
  input  [7:0] \input ,
  output [7:0] out_2
);
endmodule
