// Logisim project holy-cross-3.8.0.circ as structural Verilog: 1 circuit, main circuit main
module main (
  input  in_1
);

  Register register_1 ();  // open: D, en, Q, clk, clr
  Multiplexer multiplexer_1 ();  // open: in0, in1, out, sel, en
  Decoder decoder_1 ();  // open: out0, out1, sel, en

  // Notes on the sheet:
  //   in_1: pull=down
endmodule
