// Logisim project hierarchy.circ as structural Verilog: 2 circuits, main circuit LegacyHierarchy
module LegacyHierarchy (
  input  A,
  output Y
);

  Invert invert_1 (.A(A), .Y(Y));
endmodule

module Invert (
  input  A,
  output Y
);

  not not_1 (Y, A);
endmodule
