// Logisim project latch.circ as structural Verilog: 1 circuit, main circuit LegacyLatch
module LegacyLatch (
  input  R,
  input  S,
  output Q
);

  wire nor_2_out;

  nor nor_1 (Q, R, nor_2_out);
  nor nor_2 (nor_2_out, Q, S);
endmodule
