// Logisim project rom.circ as structural Verilog: 1 circuit, main circuit main
module main (
  input  SEL,
  output [7:0] Y
);

  ROM rom_1 (.addr({8{1'b0}}), .data(Y), .sel(SEL));

  // Notes on the sheet:
  //   contents of rom_1 (hex, n*v repeats v):
  //   a5
endmodule
