// Logisim project bus-conflict.circ as structural Verilog: 1 circuit, main circuit BusConflict
module BusConflict (
  input  [3:0] A,
  input  [3:0] B,
  output [3:0] Y
);


  assign B = A;
  assign Y = A;
endmodule
