// Logisim project derived-clock-feedback.circ as structural Verilog: 1 circuit, main circuit DerivedClockFeedback
module DerivedClockFeedback (
  input  CLK,
  input  SET,
  input  RST
);

  wire d_ff_1_q, not_1_out, not_2_out;

  not not_1 (not_1_out, CLK);
  D_Flip_Flop d_ff_1 (.clk(not_1_out), .D(not_2_out), .Q(d_ff_1_q), .preset(SET), .reset(RST));  // open: Qn
  not not_2 (not_2_out, d_ff_1_q);
endmodule
