// Logisim project ram-feedback.circ as structural Verilog: 1 circuit, main circuit RamFeedback
module RamFeedback (
  input  CLR,
  input  [1:0] ADDR,
  input  WE,
  input  OE,
  input  CLK
);

  wire not_1_out, not_2_out, ram_1_dout;

  RAM #(.addrWidth(2), .dataWidth(1), .databus("bibus"), .enables("byte"), .trigger("rising"), .asyncread("true"), .clearpin("true")) ram_1 (
    .addr(ADDR), .we(WE), .oe(OE), .clk(not_1_out), .din(not_2_out), .dout(ram_1_dout), .clr(CLR));
  not not_1 (not_1_out, CLK);
  not not_2 (not_2_out, ram_1_dout);
endmodule
