// Logisim project register-input-tail.circ as structural Verilog: 1 circuit, main circuit main
module main (
  input  [7:0] D,
  input  CLK,
  output [7:0] Q
);

  Register #(.width(8)) register_1 (.D(D), .Q(Q), .clk(CLK));  // open: en, clr
endmodule
