// Logisim project simultaneous-registers.circ as structural Verilog: 1 circuit, main circuit SimultaneousRegisters
module SimultaneousRegisters (
  input  [3:0] DATA,
  input  EN1,
  input  EN2,
  input  RST1,
  input  RST2,
  input  CLK
);

  wire [3:0] register_1_q;

  Register #(.width(4)) register_1 (.D(DATA), .en(EN1), .Q(register_1_q), .clk(CLK), .clr(RST1));
  Register #(.width(4)) register_2 (.D(register_1_q), .en(EN2), .clk(CLK), .clr(RST2));  // open: Q
endmodule
