// Logisim project subcircuit-ripple.circ as structural Verilog: 2 circuits, main circuit add8
module fa (
  input  a,
  input  b,
  input  cin,
  output s,
  output cout
);

  wire c1, c2, x1;

  xor xor_1 (x1, a, b);
  and and_1 (c1, a, b);
  xor xor_2 (s, x1, cin);
  and and_2 (c2, x1, cin);
  or or_1 (cout, c1, c2);
endmodule

module add8 (
  input  a0,
  input  a1,
  input  a2,
  input  a3,
  input  a4,
  input  a5,
  input  a6,
  input  a7,
  input  b0,
  input  b1,
  input  b2,
  input  b3,
  input  b4,
  input  b5,
  input  b6,
  input  b7,
  input  cin,
  output s0,
  output s1,
  output s2,
  output s3,
  output s4,
  output s5,
  output s6,
  output s7,
  output cout
);

  wire c1, c2, c3, c4, c5, c6, c7;

  fa fa_1 (.a(a0), .b(b0), .cin(cin), .s(s0), .cout(c1));
  fa fa_2 (.a(a1), .b(b1), .cin(c1), .s(s1), .cout(c2));
  fa fa_3 (.a(a2), .b(b2), .cin(c2), .s(s2), .cout(c3));
  fa fa_4 (.a(a3), .b(b3), .cin(c3), .s(s3), .cout(c4));
  fa fa_5 (.a(a4), .b(b4), .cin(c4), .s(s4), .cout(c5));
  fa fa_6 (.a(a5), .b(b5), .cin(c5), .s(s5), .cout(c6));
  fa fa_7 (.a(a6), .b(b6), .cin(c6), .s(s6), .cout(c7));
  fa fa_8 (.a(a7), .b(b7), .cin(c7), .s(s7), .cout(cout));

  // Other names for the same wires on the sheet: c0 = cin; c8 = cout
endmodule
