// Logisim project net-errors.circ as structural Verilog: 1 circuit, main circuit main
module main (
  input  [7:0] A,
  input  [7:0] B,
  input  [7:0] Wide,
  output [7:0] Conflict,
  output [3:0] Narrow
);

  // NOT_Gate Unconnected is placed but not wired
  // Pins of 4 and 8 bits meet at Wide

  assign B = A;
  assign Narrow = Wide[3:0];

  // Notes on the sheet:
  //   A: initial=0x0f
  //   B: initial=0x07
endmodule
