// Logisim project extra-converters.circ as structural Verilog: 1 circuit, main circuit BFH_converters
module BFH_converters (
  output segment_f,
  output segment_a,
  output segment_g,
  output segment_b,
  output [3:0] hundreds,
  output [3:0] tens,
  output [3:0] ones,
  output segment_e,
  output segment_c,
  output segment_d
);

  // Binary_to_BCD_converter #(.binvalue(9)) binary_to_bcd_converter_1: pin names not known; wires that end beside it: 9'h141, hundreds, tens
  // BCD_to_7_Segment_decoder bcd_to_7_segment_decoder_1: pin names not known; wires that end beside it: segment_g, segment_e, segment_f, segment_d, ones, segment_a, segment_c, segment_b
endmodule
