// Logisim project floating-point.circ as structural Verilog: 4 circuits, main circuit FP32
module FP8 (
  output [7:0] Sum,
  output NaN
);

  wire [7:0] fpconstant_1_p1, fpconstant_2_p1;

  // FPConstant #(.fpwidth(8), .value(3.0)) fpconstant_1: pin names not known; wires that end beside it: fpconstant_1_p1
  // FPConstant #(.fpwidth(8), .value(2.0)) fpconstant_2: pin names not known; wires that end beside it: fpconstant_2_p1, NaN
  FPAdder #(.fpwidth(8)) fpadder_1 (.a(fpconstant_1_p1), .b(fpconstant_2_p1), .out(Sum));
endmodule

module FP16 (
  output [15:0] Sum,
  output NaN
);

  wire [15:0] fpconstant_1_p1, fpconstant_2_p1;

  // FPConstant #(.fpwidth(16), .value(3.0)) fpconstant_1: pin names not known; wires that end beside it: fpconstant_1_p1
  // FPConstant #(.fpwidth(16), .value(2.0)) fpconstant_2: pin names not known; wires that end beside it: fpconstant_2_p1, NaN
  FPAdder #(.fpwidth(16)) fpadder_1 (.a(fpconstant_1_p1), .b(fpconstant_2_p1), .out(Sum));
endmodule

module FP32 (
  output [31:0] Sum,
  output NaN
);

  wire [31:0] fpconstant_1_p1, fpconstant_2_p1;

  // FPConstant #(.fpwidth(32), .value(3.0)) fpconstant_1: pin names not known; wires that end beside it: fpconstant_1_p1
  // FPConstant #(.fpwidth(32), .value(2.0)) fpconstant_2: pin names not known; wires that end beside it: fpconstant_2_p1, NaN
  FPAdder #(.fpwidth(32)) fpadder_1 (.a(fpconstant_1_p1), .b(fpconstant_2_p1), .out(Sum));
endmodule

module FP64 (
  output [63:0] Sum,
  output NaN
);

  wire [63:0] fpconstant_1_p1, fpconstant_2_p1;

  // FPConstant #(.fpwidth(64), .value(3.0)) fpconstant_1: pin names not known; wires that end beside it: fpconstant_1_p1
  // FPConstant #(.fpwidth(64), .value(2.0)) fpconstant_2: pin names not known; wires that end beside it: fpconstant_2_p1, NaN
  FPAdder #(.fpwidth(64)) fpadder_1 (.a(fpconstant_1_p1), .b(fpconstant_2_p1), .out(Sum));
endmodule
