// Logisim project mobile-evolution-true-true-false.circ as structural Verilog
module main (
  input  in_1
);

  D_Flip_Flop #(.trigger("rising")) d_ff_1 ();  // open: clk, D, Q, Qn, preset, reset
endmodule
