// Logisim project mobile-logisim_evolution-true-true-true.circ as structural Verilog
module main (
  input  in_1
);

  D_Flip_Flop #(.trigger("rising")) d_ff_1 ();  // open: D, clk, Q, Qn, preset, reset
endmodule
