// Logisim project mobile-demo.circ as structural Verilog: 1 circuit, main circuit Minha_primeira_porta_AND
module Minha_primeira_porta_AND (
  input  A,
  input  B,
  output Y
);

  and AND (Y, A, B);
endmodule
