// Logisim project mobile-example-d-flip-flop.circ as structural Verilog: 1 circuit, main circuit DMemory
module DMemory (
  input  D,
  input  CLK,
  input  CLR,
  output Q
);

  D_Flip_Flop #(.trigger("rising")) d_ff_1 (.clk(CLK), .D(D), .Q(Q), .reset(CLR));  // open: Qn, preset
endmodule
