// Logisim project mobile-example-hierarchy.circ as structural Verilog: 2 circuits, main circuit Hierarchy
module Hierarchy (
  input  A,
  output Y
);

  Inversor inversor_1 (.Entrada(A), .Y(Y));
endmodule

module Inversor (
  input  Entrada,
  output Y
);

  not not_1 (Y, Entrada);
endmodule
