// Logisim project drc-gated.circ as structural Verilog: 1 circuit, main circuit main
module main (
  input  u_data,
  output u_result
);

  wire u_clock_out, u_gate_out;

  Clock #(.highDuration(1), .lowDuration(1), .phaseOffset(0)) u_clock (.out(u_clock_out));
  D_Flip_Flop #(.trigger("rising")) u_flip (.clk(u_gate_out), .D(u_data), .Q(u_result));  // open: Qn, preset, reset
  buf u_gate (u_gate_out, u_clock_out);  // AND_Gate
endmodule
