// Logisim project drc-pin-clock.circ as structural Verilog: 1 circuit, main circuit main
module main (
  input  u_clk,
  input  u_data,
  output u_result
);

  D_Flip_Flop #(.trigger("rising")) u_flip (.clk(u_clk), .D(u_data), .Q(u_result));  // open: Qn, preset, reset
endmodule
