// Logisim project all-components.circ as structural Verilog: 1 circuit, main circuit main
module main (
);

  // SocBus #(.SocBusIdentifier("test-bus")) socbus_1: pin names not known
  // Socmem #(.SocBusSelection("test-bus")) socmem_1: pin names not known
  // SocPio #(.SocBusSelection("test-bus"), .width(4), .direction("bidir"), .genirq("true")) socpio_1: pin names not known
  // SocVga #(.SocBusSelection("test-bus")) socvga_1: pin names not known
  // SocDma #(.SocBusSelection("test-bus")) socdma_1: pin names not known
  // SocJtagUart #(.SocBusSelection("test-bus")) socjtaguart_1: pin names not known
  // Rv32im #(.SocBusSelection("test-bus"), .irqWidth(2)) rv32im_1: pin names not known
  // Nios2 #(.SocBusSelection("test-bus"), .irqWidth(2)) nios2_1: pin names not known
endmodule
