// Logisim project program-nios2.circ as structural Verilog: 1 circuit, main circuit main
module main (
);

  // SocBus #(.SocBusIdentifier("program-bus")) socbus_1: pin names not known
  // Socmem #(.SocBusSelection("program-bus")) socmem_1: pin names not known
  // SocPio #(.SocBusSelection("program-bus"), .StartAddress('h1000), .direction("outputonly"), .width(8)) socpio_1: pin names not known
  // Nios2 #(.SocBusSelection("program-bus")) nios2_1: pin names not known
endmodule
