// Logisim project program-rv32.circ as structural Verilog: 1 circuit, main circuit main
module main (
);

  // SocBus #(.SocBusIdentifier("program-bus")) socbus_1: pin names not known
  // Socmem #(.SocBusSelection("program-bus")) socmem_1: pin names not known
  // SocPio #(.SocBusSelection("program-bus"), .StartAddress('h1000), .direction("outputonly"), .width(8)) socpio_1: pin names not known
  // Rv32im #(.SocBusSelection("program-bus")) rv32im_1: pin names not known
endmodule
