// Logisim project menu-tool.circ as structural Verilog: 2 circuits, main circuit main
module main (
  input  a
);

  // PlaRom plarom_1: pin names not known
  // AND_Gate and_1 is placed but not wired
  RAM ram_1 ();  // open: addr, data, sel, clk, ld, clr
  child child_1 ();  // open: x
  // Image image_1: pin names not known
  PLA pla_1 ();  // open: in, out
  ROM rom_1 ();  // open: addr, data
  // Rv32im rv32im_1: pin names not known
  // Nios2 cpu2: pin names not known
  // SocBus socbus_1: pin names not known
  // SocPio socpio_1: pin names not known
  // SocVga socvga_1: pin names not known
  // Socmem socmem_1: pin names not known

  // Notes on the sheet:
  //   note
endmodule

module child (
  input  x
);
endmodule
