// Logisim project poke-pins.circ as structural Verilog: 1 circuit, main circuit main
module main (
  input  p1,
  input  t1,
  input  [3:0] b4,
  input  [7:0] h8,
  input  [2:0] t3
);
endmodule
