// Logisim project bench-pass.circ as structural Verilog
module logisim_test_verif (
  output test_bench_done_o,
  output test_bench_ok_o
);

  Clock clock_1 (.out(test_bench_done_o));

  assign test_bench_ok_o = test_bench_done_o;
endmodule
