// Logisim project memory.circ as structural Verilog: 1 circuit, main circuit main
module main (
  output [7:0] D,
  output halt,
  output [7:0] R
);

  wire clock_1_out;
  wire [2:0] counter_1_q;

  Counter #(.width(3), .max('h5)) counter_1 (
    .Q(counter_1_q), .carry(halt), .clk(clock_1_out));  // open: load, D, count, up, clr
  Clock clock_1 (.out(clock_1_out));
  RAM #(.addrWidth(3), .dataWidth(8)) mem (.addr(counter_1_q), .dout(D));  // open: we, oe, clk, din
  ROM #(.addrWidth(3), .dataWidth(8)) code (.addr(counter_1_q), .data(R));

  // Notes on the sheet:
  //   contents of code (hex, n*v repeats v):
  //   9 8 7 6 5 4 3 2
endmodule
