// Logisim project main.circ as structural Verilog: 2 circuits, main circuit main
module main (
  input  A,
  output Y
);

  \cell  cell_1 (.a(A), .y(Y));
endmodule

module top (
  input  B,
  output Z
);


  assign Z = B;
endmodule
