// Logisim project tty.circ as structural Verilog: 1 circuit, main circuit main
module main (
  output halt
);

  wire clock_1_out;
  wire [2:0] counter_1_q;
  wire [6:0] rom_1_data;

  Counter #(.width(3), .max('h5)) counter_1 (
    .Q(counter_1_q), .carry(halt), .clk(clock_1_out));  // open: load, D, count, up, clr
  Clock clock_1 (.out(clock_1_out));
  ROM #(.addrWidth(3), .dataWidth(7)) rom_1 (.addr(counter_1_q), .data(rom_1_data));
  TTY tty_1 (.data(rom_1_data), .clk(clock_1_out), .we(1'b1));  // open: clr

  // Notes on the sheet:
  //   contents of rom_1 (hex, n*v repeats v):
  //   48 69 21 a 4f 4b 0 0
endmodule
