// Logisim project fpga-comb.circ as structural Verilog: 1 circuit, main circuit main
module main (
  input  a,
  input  b,
  input  c,
  input  d,
  output y,
  output z,
  output w
);

  and and_1 (y, a, b);
  // XOR_Gate xor_1 has open pins: out=z
  // NOR_Gate nor_1 has open pins: out=w
endmodule
