// Logisim project drivers.circ as structural Verilog: 1 circuit, main circuit main
module main (
);

  // SocPio #(.width(8), .direction("bidir"), .genirq("true"), .inputssynccapt("true"), .outputbitsetclear("true")) pio_bidir: pin names not known
  // SocPio #(.width(4), .direction("inputonly"), .genirq("true"), .inputssynccapt("true"), .outputbitsetclear("true")) pio_in: pin names not known
  // SocPio #(.width(4), .direction("outputonly"), .outputbitsetclear("true")) pio_out: pin names not known
  // SocPio #(.width(4), .direction("inout"), .inputssynccapt("true"), .outputbitsetclear("true")) pio_inout: pin names not known
  // SocPio #(.width(2), .direction("inputonly")) pio_plain: pin names not known
endmodule
