// Logisim project assembly-counters.circ as structural Verilog: 1 circuit, main circuit main
module main (
);

  wire clock_1_out, clock_2_out, clock_3_out, clock_4_out, clock_5_out, clock_6_out;
  wire [7:0] adder_1_out, adder_4_out, PC_q, register_1_q, UND_q;
  wire [11:0] ACC_q, adder_5_out;
  wire [15:0] adder_2_out, ADDR_q;
  wire [31:0] adder_3_out, BIG_q;

  Adder #(.width(8)) adder_1 (.a(PC_q), .b(8'h1), .out(adder_1_out));  // open: cin, cout
  Adder #(.width(16)) adder_2 (.a(ADDR_q), .b(16'hb), .out(adder_2_out));  // open: cin, cout
  Adder #(.width(32)) adder_3 (.a(BIG_q), .b(32'h10001), .out(adder_3_out));  // open: cin, cout
  Adder #(.width(8)) adder_4 (.a(register_1_q), .b(8'h3), .out(adder_4_out));  // open: cin, cout
  Adder #(.width(12)) adder_5 (.a(ACC_q), .b(12'h25), .out(adder_5_out));  // open: cin, cout
  Register #(.width(8)) PC (.D(adder_1_out), .Q(PC_q), .clk(clock_1_out));  // open: en, clr
  Clock clock_1 (.out(clock_1_out));
  Register #(.width(16)) ADDR (.D(adder_2_out), .Q(ADDR_q), .clk(clock_2_out));  // open: en, clr
  Clock clock_2 (.out(clock_2_out));
  Register #(.width(32)) BIG (.D(adder_3_out), .Q(BIG_q), .clk(clock_3_out));  // open: en, clr
  Clock clock_3 (.out(clock_3_out));
  Register #(.width(8)) register_1 (.D(adder_4_out), .Q(register_1_q), .clk(clock_4_out));  // open: en, clr
  Clock clock_4 (.out(clock_4_out));
  Register #(.width(8)) UND (.Q(UND_q), .clk(clock_5_out));  // open: D, en, clr
  Clock clock_5 (.out(clock_5_out));
  Register #(.width(12)) ACC (.D(adder_5_out), .Q(ACC_q), .clk(clock_6_out));  // open: en, clr
  Clock clock_6 (.out(clock_6_out));
endmodule
