// Logisim project appearance.circ as structural Verilog: 2 circuits, main circuit evo
module evo (
  input  A,
  input  B,
  output Y
);
endmodule

module classic (
  input  A,
  input  B,
  output Y
);
endmodule
