// Logisim project merge.circ as structural Verilog: 3 circuits, main circuit top
module top (
);

  leaf leaf_1 ();  // open: in_1
endmodule

module leaf (
  input  in_1
);

  // NOT_Gate not_1 has open pins: in=in_1, out=open
endmodule

module unused (
);

  // OR_Gate or_1 is placed but not wired
endmodule
