// Logisim project project.circ as structural Verilog: 3 circuits, main circuit main
module main (
  input  A,
  input  B,
  output S
);

  wire and_1_out;

  // half half_1: pin names not known; wires that end beside it: A, B, S
  // AND_Gate and_1 has open pins: out=and_1_out
  // NOT_Gate not_1 has open pins: in=and_1_out, out=open

  // Notes on the sheet:
  //   menus
endmodule

module half (
  input  A,
  input  B,
  output S,
  output C
);

  xor xor_1 (S, A, B);
  and and_1 (C, A, B);
endmodule

module spare (
);

  // OR_Gate or_1 is placed but not wired
endmodule
