// Logisim project sim.circ as structural Verilog: 2 circuits, main circuit main
module main (
  output q0
);

  wire clock_1_out, d_ff_1_qn;

  Clock clock_1 (.out(clock_1_out));
  D_Flip_Flop d_ff_1 (.D(d_ff_1_qn), .clk(clock_1_out), .Q(q0), .Qn(d_ff_1_qn));  // open: preset, reset
  stage stage_1 (.clk(d_ff_1_qn));  // open: q
endmodule

module stage (
  input  clk,
  output q
);

  wire d_ff_1_qn;

  D_Flip_Flop d_ff_1 (.D(d_ff_1_qn), .clk(clk), .Q(q), .Qn(d_ff_1_qn));  // open: preset, reset
endmodule
