// Logisim project step.circ as structural Verilog: 1 circuit, main circuit main
module main (
  input  A,
  output Y
);

  wire not_1_out, not_2_out;

  not not_1 (not_1_out, A);
  not not_2 (not_2_out, not_1_out);
  not not_3 (Y, not_2_out);
endmodule
