// Logisim project svg-gates.circ as structural Verilog: 1 circuit, main circuit main
module main (
);

  wire and_1_out, or_1_out, xor_1_out;

  // AND_Gate and_1 has open pins: out=and_1_out
  // OR_Gate or_1 has open pins: out=or_1_out
  xor xor_1 (xor_1_out, and_1_out, or_1_out);
  // NOT_Gate not_1 has open pins: in=xor_1_out, out=open
endmodule
