// Logisim project svg-labels.circ as structural Verilog: 1 circuit, main circuit main
module main (
);

  // AND_Gate ande is placed but not wired
  // AND_Gate andw is placed but not wired
  // AND_Gate andn is placed but not wired
  // AND_Gate ands is placed but not wired
  // NAND_Gate nande is placed but not wired
  // NAND_Gate nandw is placed but not wired
  // NAND_Gate nandn is placed but not wired
  // NAND_Gate nands is placed but not wired
  // XOR_Gate xore is placed but not wired
  // XOR_Gate xorw is placed but not wired
  // XOR_Gate xorn is placed but not wired
  // XOR_Gate xors is placed but not wired
  // OR_Gate ore is placed but not wired
  // OR_Gate orw is placed but not wired
  // OR_Gate orn is placed but not wired
  // OR_Gate ors is placed but not wired
  // NOT_Gate note is placed but not wired
  // NOT_Gate notw is placed but not wired
  // NOT_Gate notn is placed but not wired
  // NOT_Gate nots is placed but not wired
  // Buffer bufe is placed but not wired
  // Buffer bufw is placed but not wired
  // Buffer bufn is placed but not wired
  // Buffer bufs is placed but not wired
  Controlled_Buffer cbre ();  // open: in, out, en
  Controlled_Buffer cbrw ();  // open: in, out, en
  Controlled_Buffer cbrn ();  // open: in, out, en
  Controlled_Buffer cbrs ();  // open: in, out, en
  Controlled_Inverter cile ();  // open: in, out, en
  Controlled_Inverter cilw ();  // open: in, out, en
  Controlled_Inverter ciln ();  // open: in, out, en
  Controlled_Inverter cils ();  // open: in, out, en
  // Odd_Parity odde is placed but not wired
  // Even_Parity evenw is placed but not wired
  // Odd_Parity odd_parity_1 is placed but not wired
endmodule
