// Logisim project svg-printer.circ as structural Verilog: 1 circuit, main circuit main
module main (
  input  in_1
);

  wire undriven, undriven_2;

  // OR_Gate or_1 has open pins: in0=undriven, out=open
  // OR_Gate or_2 has open pins: in1=undriven_2, out=open
  // XOR_Gate xor_1 has open pins: in1=in_1, out=open
  // NOR_Gate nor_1 is placed but not wired
endmodule
