// Logisim project wavedrom.circ as structural Verilog: 1 circuit, main circuit main
module main (
  output open,
  output [3:0] q,
  output carry
);

  wire clk_out;

  Counter #(.width(4), .max('hf)) counter_1 (.Q(q), .carry(carry), .clk(clk_out));  // open: load, D, count, up, clr
  Clock clk (.out(clk_out));
endmodule
